# Fritzing sketch wiring (saved by Fritzing 0.9.4)
breadboards: 2

parts:
  CONN1 = USB connector [package=THT]
  IC1 = IC, DIP package, 14 pins [chip_label=MCP2221A]
  C2 = Ceramic Capacitor [capacitance=0.22µF voltage=16V package="100 mil [THT, multilayer]"]
  C3 = Ceramic Capacitor [capacitance=0.1µF voltage=16V package="100 mil [THT, multilayer]"]
  R3 = Resistor [tolerance=±5% resistance=10k package=THT]
  R10 = Resistor [tolerance=±5% resistance=470 package=THT]
  R11 = Resistor [tolerance=±5% resistance=470 package=THT]
  R12 = Resistor [tolerance=±5% resistance=470 package=THT]
  R13 = Resistor [tolerance=±5% resistance=470 package=THT]
  R14 = Resistor [tolerance=±5% resistance=470 package=THT]
  R15 = Resistor [tolerance=±5% resistance=470 package=THT]
  R16 = Resistor [tolerance=±5% resistance=470 package=THT]
  R17 = Resistor [tolerance=±5% resistance=470 package=THT]
  R18 = Resistor [tolerance=±5% resistance=470 package=THT]
  R19 = Resistor [tolerance=±5% resistance=470 package=THT]
  R20 = Resistor [tolerance=±5% resistance=470 package=THT]
  R21 = Resistor [tolerance=±5% resistance=470 package=THT]
  R22 = Resistor [tolerance=±5% resistance=470 package=THT]
  R23 = Resistor [tolerance=±5% resistance=470 package=THT]
  R24 = Resistor [tolerance=±5% resistance=470 package=THT]
  R25 = Resistor [tolerance=±5% resistance=470 package=THT]
  LED5 = LED - 5mm [color="Red (633nm)" package="5 mm [THT]"]
  LED6 = LED - 5mm [color="Red (633nm)" package="5 mm [THT]"]
  LED7 = LED - 5mm [color="Red (633nm)" package="5 mm [THT]"]
  ↓LED_1-QH = LED - 5mm [color="Red (633nm)" package="5 mm [THT]"]
  ↓LED_2-QA = LED - 5mm [color="Red (633nm)" package="5 mm [THT]"]
  LED10 = LED - 5mm [color="Red (633nm)" package="5 mm [THT]"]
  LED11 = LED - 5mm [color="Red (633nm)" package="5 mm [THT]"]
  LED12 = LED - 5mm [color="Red (633nm)" package="5 mm [THT]"]
  LED13 = LED - 5mm [color="Red (633nm)" package="5 mm [THT]"]
  LED14 = LED - 5mm [color="Red (633nm)" package="5 mm [THT]"]
  LED15 = LED - 5mm [color="Red (633nm)" package="5 mm [THT]"]
  ↓LED_2-QH = LED - 5mm [color="Red (633nm)" package="5 mm [THT]"]
  ↓LED_1-QA = LED - 5mm [color="Red (633nm)" package="5 mm [THT]"]
  LED18 = LED - 5mm [color="Red (633nm)" package="5 mm [THT]"]
  LED19 = LED - 5mm [color="Red (633nm)" package="5 mm [THT]"]
  LED20 = LED - 5mm [color="Red (633nm)" package="5 mm [THT]"]
  74HC595-1 = IC, DIP package, 16 pins [chip_label=74HC595]
  74HC595-2 = IC, DIP package, 16 pins [chip_label=74HC595]
  C4 = Ceramic Capacitor [capacitance=0.1µF voltage=16V package="100 mil [THT, multilayer]"]
  C5 = Ceramic Capacitor [capacitance=0.1µF voltage=16V package="100 mil [THT, multilayer]"]

nets:
  N1: CONN1.5V, IC1.pin1, R3.Pin_0, 74HC595-1.pin10, 74HC595-1.pin16, 74HC595-2.pin10, 74HC595-2.pin16, C4.0, C5.0
  N2: CONN1.d-, IC1.pin12
  N3: CONN1.d+, IC1.pin13
  N4: CONN1.GND, CONN1.chassis5, CONN1.chassis6, IC1.pin14, C2.0, C3.1, 74HC595-1.pin8, 74HC595-1.pin13, 74HC595-2.pin8, 74HC595-2.pin13, C4.1, C5.1
  N5: IC1.pin2, 74HC595-1.pin12, 74HC595-2.pin12
  N6: IC1.pin3, 74HC595-1.pin11, 74HC595-2.pin11
  N7: IC1.pin4, C3.0, R3.Pin_1
  N8: IC1.pin7, 74HC595-1.pin14
  N9: IC1.pin11, C2.1
  N10: R10.Pin_0, LED5.anode
  N11: R10.Pin_1, 74HC595-1.pin4
  N12: R11.Pin_0, LED18.anode
  N13: R11.Pin_1, 74HC595-1.pin1
  N14: R12.Pin_0, LED19.anode
  N15: R12.Pin_1, 74HC595-1.pin2
  N16: R13.Pin_0, LED20.anode
  N17: R13.Pin_1, 74HC595-1.pin3
  N18: R14.Pin_0, ↓LED_1-QA.anode
  N19: R14.Pin_1, 74HC595-1.pin15
  N20: R15.Pin_0, LED6.anode
  N21: R15.Pin_1, 74HC595-1.pin5
  N22: R16.Pin_0, LED7.anode
  N23: R16.Pin_1, 74HC595-1.pin6
  N24: R17.Pin_0, ↓LED_1-QH.anode
  N25: R17.Pin_1, 74HC595-1.pin7
  N26: R18.Pin_0, ↓LED_2-QA.anode
  N27: R18.Pin_1, 74HC595-2.pin15
  N28: R19.Pin_0, LED11.anode
  N29: R19.Pin_1, 74HC595-2.pin2
  N30: R20.Pin_0, LED10.anode
  N31: R20.Pin_1, 74HC595-2.pin1
  N32: R21.Pin_0, LED12.anode
  N33: R21.Pin_1, 74HC595-2.pin3
  N34: R22.Pin_0, LED15.anode
  N35: R22.Pin_1, 74HC595-2.pin6
  N36: R23.Pin_0, ↓LED_2-QH.anode
  N37: R23.Pin_1, 74HC595-2.pin7
  N38: R24.Pin_0, LED14.anode
  N39: R24.Pin_1, 74HC595-2.pin5
  N40: R25.Pin_0, LED13.anode
  N41: R25.Pin_1, 74HC595-2.pin4
  N42: LED5.cathode, LED6.cathode, LED7.cathode, ↓LED_1-QH.cathode, ↓LED_2-QA.cathode, LED10.cathode, LED11.cathode, LED12.cathode, LED13.cathode, LED14.cathode, LED15.cathode, ↓LED_2-QH.cathode, ↓LED_1-QA.cathode, LED18.cathode, LED19.cathode, LED20.cathode
  N43: 74HC595-1.pin9, 74HC595-2.pin14

notes:
  D-
  D+
  VBUS
  GND
  ←PC
