# Fritzing sketch wiring (saved by Fritzing 0.9.4)
breadboards: 1

parts:
  CONN1 = USB connector [package=THT]
  IC1 = IC, DIP package, 14 pins [chip_label=MCP2221A]
  C2 = Ceramic Capacitor [capacitance=0.22µF voltage=16V package="100 mil [THT, multilayer]"]
  C3 = Ceramic Capacitor [capacitance=0.1µF voltage=16V package="100 mil [THT, multilayer]"]
  R3 = Resistor [tolerance=±5% resistance=10k package=THT]
  LED_GP0 = LED - 5mm [color="Green (565nm)" package="5 mm [THT]"]
  R4 = Resistor [tolerance=±5% resistance=470 package=THT]
  LED_GP1 = LED - 5mm [color="Green (565nm)" package="5 mm [THT]"]
  LED_GP2 = LED - 5mm [color="Green (565nm)" package="5 mm [THT]"]
  LED_GP3 = LED - 5mm [color="Green (565nm)" package="5 mm [THT]"]
  R5 = Resistor [tolerance=±5% resistance=470 package=THT]
  R6 = Resistor [tolerance=±5% resistance=470 package=THT]
  R7 = Resistor [tolerance=±5% resistance=470 package=THT]

nets:
  N1: CONN1.5V, IC1.pin1, R3.Pin_0
  N2: CONN1.d-, IC1.pin12
  N3: CONN1.d+, IC1.pin13
  N4: CONN1.GND, CONN1.chassis5, CONN1.chassis6, IC1.pin14, C2.0, C3.1, LED_GP0.cathode, LED_GP1.cathode, LED_GP2.cathode, LED_GP3.cathode
  N5: IC1.pin2, R4.Pin_1
  N6: IC1.pin3, R5.Pin_1
  N7: IC1.pin4, C3.0, R3.Pin_1
  N8: IC1.pin7, R6.Pin_1
  N9: IC1.pin8, R7.Pin_1
  N10: IC1.pin11, C2.1
  N11: LED_GP0.anode, R4.Pin_0
  N12: LED_GP1.anode, R5.Pin_0
  N13: LED_GP2.anode, R6.Pin_0
  N14: LED_GP3.anode, R7.Pin_0

notes:
  D-
  D+
  VBUS
  GND
  ←PC
