# Fritzing sketch wiring (saved by Fritzing 0.9.4)
breadboards: 1

parts:
  CONN1 = USB connector [package=THT]
  IC1 = IC, DIP package, 14 pins [chip_label=MCP2221A]
  C2 = Ceramic Capacitor [capacitance=0.22µF voltage=16V package="100 mil [THT, multilayer]"]
  C3 = Ceramic Capacitor [capacitance=0.1µF voltage=16V package="100 mil [THT, multilayer]"]
  REG_3_3V = Voltage Regulator - 3.3V [package="TO220 [THT]"]
  C4 = Ceramic Capacitor [capacitance=0.1µF voltage=16V package="100 mil [THT, multilayer]"]
  C5 = Electrolytic Capacitor [capacitance=47µF voltage=35V package="100 mil [THT, electrolytic]"]
  R3 = Resistor [tolerance=±5% resistance=10k package=THT]
  パーツ1 = BME280 Breakout
  R5 = Resistor [tolerance=±5% resistance=4.7k package=THT]
  R6 = Resistor [tolerance=±5% resistance=4.7k package=THT]

nets:
  N1: CONN1.5V, IC1.pin6, REG_3_3V.input_voltage, C4.0
  N2: CONN1.d-, IC1.pin12
  N3: CONN1.d+, IC1.pin13
  GND: CONN1.GND, CONN1.chassis5, CONN1.chassis6, IC1.pin14, C2.0, C3.1, REG_3_3V.GND, C4.1, C5.-, パーツ1.GND
  N4: IC1.pin1, R3.Pin_0
  N5: IC1.pin4, C3.0, R3.Pin_1
  N6: IC1.pin9, パーツ1.SDI/SDA, R5.Pin_1
  N7: IC1.pin10, パーツ1.SCK/SCL, R6.Pin_1
  N8: IC1.pin11, C2.1, REG_3_3V.output_voltage, C5.+, パーツ1.3.3V, R5.Pin_0, R6.Pin_0

notes:
  D-
  D+
  3.3V
  VBUS
  GND
  ←PC
  SCL
  SDA
