# Fritzing sketch wiring (saved by Fritzing 0.9.4)
breadboards: 2

parts:
  CONN1 = USB connector [package=THT]
  IC1 = IC, DIP package, 14 pins [chip_label=MCP2221A]
  C2 = Ceramic Capacitor [capacitance=0.22µF voltage=16V package="100 mil [THT, multilayer]"]
  C3 = Ceramic Capacitor [capacitance=0.1µF voltage=16V package="100 mil [THT, multilayer]"]
  R3 = Resistor [tolerance=±5% resistance=10k package=THT]
  IC2 = IC, DIP package, 28 pins [chip_label=MCP23017]
  C4 = Ceramic Capacitor [capacitance=0.1µF voltage=16V package="100 mil [THT, multilayer]"]
  C5 = Electrolytic Capacitor [capacitance=100µF voltage=16V package="100 mil [THT, electrolytic]"]
  C6 = Ceramic Capacitor [capacitance=0.1µF voltage=16V package="100 mil [THT, multilayer]"]
  R7 = Resistor [tolerance=±5% resistance=10k package=THT]
  R8 = Resistor [tolerance=±5% resistance=10k package=THT]
  R9 = Resistor [tolerance=±5% resistance=10k package=THT]
  R10 = Resistor [tolerance=±5% resistance=470 package=THT]
  R11 = Resistor [tolerance=±5% resistance=470 package=THT]
  R12 = Resistor [tolerance=±5% resistance=470 package=THT]
  R13 = Resistor [tolerance=±5% resistance=470 package=THT]
  R14 = Resistor [tolerance=±5% resistance=470 package=THT]
  R15 = Resistor [tolerance=±5% resistance=470 package=THT]
  R16 = Resistor [tolerance=±5% resistance=470 package=THT]
  R17 = Resistor [tolerance=±5% resistance=470 package=THT]
  R18 = Resistor [tolerance=±5% resistance=470 package=THT]
  R19 = Resistor [tolerance=±5% resistance=470 package=THT]
  R20 = Resistor [tolerance=±5% resistance=470 package=THT]
  R21 = Resistor [tolerance=±5% resistance=470 package=THT]
  R22 = Resistor [tolerance=±5% resistance=470 package=THT]
  R23 = Resistor [tolerance=±5% resistance=470 package=THT]
  R24 = Resistor [tolerance=±5% resistance=470 package=THT]
  R25 = Resistor [tolerance=±5% resistance=470 package=THT]
  LED5 = LED - 5mm [color="Red (633nm)" package="5 mm [THT]"]
  LED6 = LED - 5mm [color="Red (633nm)" package="5 mm [THT]"]
  LED7 = LED - 5mm [color="Red (633nm)" package="5 mm [THT]"]
  ↓LED_GPA7 = LED - 5mm [color="Red (633nm)" package="5 mm [THT]"]
  ↓LED_GPB0 = LED - 5mm [color="Red (633nm)" package="5 mm [THT]"]
  LED10 = LED - 5mm [color="Red (633nm)" package="5 mm [THT]"]
  LED11 = LED - 5mm [color="Red (633nm)" package="5 mm [THT]"]
  LED12 = LED - 5mm [color="Red (633nm)" package="5 mm [THT]"]
  LED13 = LED - 5mm [color="Red (633nm)" package="5 mm [THT]"]
  LED14 = LED - 5mm [color="Red (633nm)" package="5 mm [THT]"]
  LED15 = LED - 5mm [color="Red (633nm)" package="5 mm [THT]"]
  ↓LED_GPB7 = LED - 5mm [color="Red (633nm)" package="5 mm [THT]"]
  ↓LED_GPA0 = LED - 5mm [color="Red (633nm)" package="5 mm [THT]"]
  LED18 = LED - 5mm [color="Red (633nm)" package="5 mm [THT]"]
  LED19 = LED - 5mm [color="Red (633nm)" package="5 mm [THT]"]
  LED20 = LED - 5mm [color="Red (633nm)" package="5 mm [THT]"]

nets:
  N1: CONN1.5V, IC1.pin1, R3.Pin_0, IC2.pin9, C4.0, C5.+, R8.Pin_1, R9.Pin_1
  N2: CONN1.d-, IC1.pin12
  N3: CONN1.d+, IC1.pin13
  N4: CONN1.GND, CONN1.chassis5, CONN1.chassis6, IC1.pin14, C2.0, C3.1, IC2.pin10, C4.1, C5.-
  N5: IC1.pin4, C3.0, R3.Pin_1
  N6: IC1.pin9, IC2.pin13, R9.Pin_0
  N7: IC1.pin10, IC2.pin12, R8.Pin_0
  N8: IC1.pin11, C2.1
  N9: IC2.pin1, R18.Pin_1
  N10: IC2.pin2, R20.Pin_1
  N11: IC2.pin3, R19.Pin_1
  N12: IC2.pin4, R21.Pin_1
  N13: IC2.pin5, R25.Pin_1
  N14: IC2.pin6, R24.Pin_1
  N15: IC2.pin7, R22.Pin_1
  N16: IC2.pin8, R23.Pin_1
  N17: IC2.pin18, C6.1, R7.Pin_1
  N18: IC2.pin21, R14.Pin_1
  N19: IC2.pin22, R11.Pin_1
  N20: IC2.pin23, R12.Pin_1
  N21: IC2.pin24, R13.Pin_1
  N22: IC2.pin25, R10.Pin_1
  N23: IC2.pin26, R15.Pin_1
  N24: IC2.pin27, R16.Pin_1
  N25: IC2.pin28, R17.Pin_1
  N26: R10.Pin_0, LED5.anode
  N27: R11.Pin_0, LED18.anode
  N28: R12.Pin_0, LED19.anode
  N29: R13.Pin_0, LED20.anode
  N30: R14.Pin_0, ↓LED_GPA0.anode
  N31: R15.Pin_0, LED6.anode
  N32: R16.Pin_0, LED7.anode
  N33: R17.Pin_0, ↓LED_GPA7.anode
  N34: R18.Pin_0, ↓LED_GPB0.anode
  N35: R19.Pin_0, LED11.anode
  N36: R20.Pin_0, LED10.anode
  N37: R21.Pin_0, LED12.anode
  N38: R22.Pin_0, LED15.anode
  N39: R23.Pin_0, ↓LED_GPB7.anode
  N40: R24.Pin_0, LED14.anode
  N41: R25.Pin_0, LED13.anode
  N42: LED5.cathode, LED6.cathode, LED7.cathode, ↓LED_GPA7.cathode, ↓LED_GPB0.cathode, LED10.cathode, LED11.cathode, LED12.cathode, LED13.cathode, LED14.cathode, LED15.cathode, ↓LED_GPB7.cathode, ↓LED_GPA0.cathode, LED18.cathode, LED19.cathode, LED20.cathode

notes:
  D-
  D+
  VBUS
  GND
  ←PC
  SCL
  SDA
